// Logisim project SAP1_versao5_claudio.circ as structural Verilog: 16 circuits, main circuit main
module main (
  input  [7:0] Entrada,
  input  Reset,
  output [3:0] Dados,
  output [3:0] \Dados___Endereços ,
  output out_5,
  output out_6,
  output out_7,
  output out_8,
  output out_9,
  output out_10,
  output out_11,
  output out_12
);

  wire CLK, Clock_out, controlador_sequencializador_rom_1_hlt, Cp, Ea, Ep, Eu, IncDec, lerEnt, loadTmr, Lp,
       Mul, nCE, nEi, nInt, nLa, nLb, nLi, nLm, nLo, not_1_out, not_2_out, not_3_out, not_4_out, or_1_out,
       RDnWR, \registrador_instruções_1_i4 , \registrador_instruções_1_i5 , \registrador_instruções_1_i6 ,
       \registrador_instruções_1_i7 , Su;
  wire [3:0] rem_1_remout, timer_1_contador;
  wire [7:0] acumulador_1_a_out_ula, counter_1_q, registrador_b_1_b_dataout;

  or or_1 (or_1_out, ~nInt, Reset);  // OR_Gate
  assign CLK = not_4_out ? Clock_out : 1'bz;  // Controlled_Buffer controlled_buffer_1
  Clock Clock (.out(Clock_out));
  not not_1 (not_1_out, CLK);
  not not_2 (not_2_out, Reset);
  not not_3 (not_3_out, nCE);
  not not_4 (not_4_out, controlador_sequencializador_rom_1_hlt);
  REM rem_1 (.in_1(\Dados___Endereços ), .nLm(nLm), .CLK(CLK), .REMOut(rem_1_remout));
  Controlador_Sequencializador_ROM controlador_sequencializador_rom_1 (
    .CLK(CLK), .CLR(or_1_out), .HLT(controlador_sequencializador_rom_1_hlt), .Cp(Cp), .Ep(Ep), .nLm(nLm),
    .nCE(nCE), .nLl(nLi), .nEl(nEi), .nLa(nLa), .Ea(Ea), .Su(Su), .Eu(Eu), .nLb(nLb), .nLo(nLo),
    .I7(\registrador_instruções_1_i7 ), .I6(\registrador_instruções_1_i6 ),
    .I4(\registrador_instruções_1_i4 ), .IncDec(IncDec), .RDnWR(RDnWR), .Mul(Mul), .Lp(Lp),
    .I5(\registrador_instruções_1_i5 ), .lerEnt(lerEnt), .loadTmr(loadTmr));
  Contador_Programa contador_programa_1 (
    .Cp(Cp), .nCLK(not_1_out), .nCLR(not_2_out), .Ep(Ep), .Cp_Out(\Dados___Endereços ), .Lp(Lp),
    .Cp_In(\Dados___Endereços ));
  \Memória_RAM  \memória_ram_1  (
    .in_2(rem_1_remout), .nCE(not_3_out), .CLK(CLK), .out_6({Dados, \Dados___Endereços }), .RD_nWR(RDnWR),
    .in_1({Dados, \Dados___Endereços }));
  \Registrador_Instruções  \registrador_instruções_1  (
    .in_1({Dados, \Dados___Endereços }), .nLi(nLi), .CLK(CLK), .CLR(Reset), .nEi(nEi),
    .out_6(\Dados___Endereços ), .I4(\registrador_instruções_1_i4 ), .I5(\registrador_instruções_1_i5 ),
    .I6(\registrador_instruções_1_i6 ), .I7(\registrador_instruções_1_i7 ));
  Timer timer_1 (.CLK(CLK), .Ld(loadTmr), .Reset(nInt), .Entrada(\Dados___Endereços ), .Contador(timer_1_contador));
  Hex_Digit_Display hex_digit_display_1 (.value(timer_1_contador));  // open: dp
  Entrada_8_bits entrada_8_bits_1 (.Entrada(Entrada), .rdEnt(lerEnt), .Endereco(\Dados___Endereços ), .Dado(Dados));
  Acumulador acumulador_1 (
    .A_In({Dados, \Dados___Endereços }), .nLa(nLa), .CLK(CLK), .Ea(Ea), .A_Out_ULA(acumulador_1_a_out_ula),
    .A_Out({Dados, \Dados___Endereços }));
  Somador_Subtrator somador_subtrator_1 (
    .Su(Su), .B_data(registrador_b_1_b_dataout), .A_dataOut2({Dados, \Dados___Endereços }),
    .A_data(acumulador_1_a_out_ula), .Eu(Eu), .IncDec(IncDec), .mul(Mul));
  Registrador_B registrador_b_1 (
    .B_dataIn({Dados, \Dados___Endereços }), .B_dataOut(registrador_b_1_b_dataout), .nLb(nLb), .CLK(CLK));
  Hex_Digit_Display hex_digit_display_2 (.value({out_5, out_6, out_7, out_8}));  // open: dp
  \Indicação_Visual  \indicação_visual_1  (
    .Input({Dados, \Dados___Endereços }),
    .Output({out_5, out_6, out_7, out_8, out_9, out_10, out_11, out_12}), .nLo(nLo), .CLK(CLK), .CLR(Reset));
  Counter counter_1 (.Q(counter_1_q), .clk(CLK), .clr(Reset));  // open: load, D, count, carry
  Hex_Digit_Display hex_digit_display_3 (.value({out_9, out_10, out_11, out_12}));  // open: dp
  Hex_Digit_Display hex_digit_display_4 (.value(counter_1_q[7:4]));  // open: dp
  Hex_Digit_Display hex_digit_display_5 (.value(counter_1_q[3:0]));  // open: dp
  DotMatrix #(.matrixcols(8), .matrixrows(1), .dotshape("circle")) dotmatrix_1 (
    .col0(out_5), .col1(out_6), .col2(out_7), .col3(out_8), .col4(out_9), .col5(out_10), .col6(out_11),
    .col7(out_12));

  // Other names for the same wires on the sheet: CLR = Reset

  // Notes on the sheet:
  //   SAP-1 EM LOGISIM Modificado Cláudio - Versão 5 2024
  //   Arquitetura de Computadores I
  //   Grupo:
  //   Instruções:
  //   LDA 0000: A<-*(MEM)
  //   ADD 0001: A<-A+B
  //   SUB 0010: A<-A-B
  //   INC 0011: A<=A+1
  //   DEC 0100: A<=A-1
  //   MUL 0101: A<-AxB
  //   JMP 0110: CP<-endereço de salto
  //   OUT 1110: exibir o valor
  //   HLT 1111: interromper o circuito
  //   INT 1000: interromper temporariamente o circuito
  //   ENT 1111: realizar entrada de dados (8 bits)
  //   Como usar:
  //   Adicione as operações no bloco de memória RAM,
  //   execute um RESET e envie pulsos de clock.
  //   Esse trabalho é uma modificação do trabalho feito por:
  //   - André Luís Silva de Paula
  //   - André Santos Alves
  //   - Nathan de Araújo Cunha Lisboa
  //   - Pedro Malta Boscatti
  //   - Sophia Damasceno Satuf
  //   As modificações foram feitas no controlador sequencializador.
  //   Com as alterações agora o controlador é implementado usando
  //   ROMs e possui ciclo variavél de máquina.
  //   Matheus Mota Cavalcante
endmodule

module Contador_Programa (
  input  Lp,
  input  [3:0] Cp_In,
  input  Cp,
  input  nCLK,
  input  nCLR,
  input  Ep,
  output [3:0] Cp_Out
);

  wire not_1_out;
  wire [3:0] counter_1_q;

  not not_1 (not_1_out, nCLR);
  Counter #(.width(4), .max('hf), .trigger("falling")) counter_1 (
    .load(Lp), .D(Cp_In), .count(Cp), .Q(counter_1_q), .clk(nCLK), .clr(not_1_out));  // open: carry
  assign Cp_Out = Ep ? counter_1_q : 4'bz;  // Controlled_Buffer controlled_buffer_1
endmodule

module REM (
  input  [3:0] in_1,
  input  nLm,
  input  CLK,
  output [3:0] REMOut
);

  wire not_1_out;

  not not_1 (not_1_out, nLm);
  Register #(.width(4)) register_1 (.D(in_1), .en(not_1_out), .Q(REMOut), .clk(CLK));  // open: clr
endmodule

module \Memória_RAM  (
  input  [7:0] in_1,
  input  [3:0] in_2,
  input  nCE,
  input  CLK,
  input  RD_nWR,
  output [7:0] out_6
);

  wire not_1_out;
  wire [7:0] controlled_buffer_1_out;

  assign controlled_buffer_1_out = not_1_out ? in_1 : 8'bz;  // Controlled_Buffer controlled_buffer_1
  assign out_6 = RD_nWR ? controlled_buffer_1_out : 8'bz;  // Controlled_Buffer controlled_buffer_2
  RAM #(.addrWidth(4)) ram_1 (
    .addr(in_2), .data(controlled_buffer_1_out), .sel(nCE), .clk(CLK), .ld(RD_nWR), .clr(1'b0));
  not not_1 (not_1_out, RD_nWR);

  // Notes on the sheet:
  //   Programas Exemplo
  //   Exemplo 1:  02 + 03 - 04 + 02 = 03
  //   0f e0 1e e0 2d e0 1f e0 f0 00 00 00 00 04 03 02
  //   Exemplo 2:  150 + 70 - 50 + 100 = ? 270
  //   0f e0 1e e0 2d e0 1c e0 f0 00 00 00 64 32 46 96
  //   Exemplo 3:  5 x 2 - 1 - 2 + 1 = 8
  //   0f e0 5e e0 40 e0 2e e0 30 e0 f0 00 00 00 02 05
  //   Exemplo 4:  Carrega A=1,Exibe A, Inc A, Exibe A, JMP para Inc A 
  //   0f e0 30 e0 62 f0
  //   Exemplo 5:  Contador Progressivo 
  //   Exemplo 6:  Gera a Série de Fibonacci 
  //    Click com o botão direito do mouse sobre a RAM e carregue alguma programação disponivel
endmodule

module \Registrador_Instruções  (
  input  [7:0] in_1,
  input  nLi,
  input  CLK,
  input  CLR,
  input  nEi,
  output [3:0] out_6,
  output I4,
  output I5,
  output I6,
  output I7
);

  wire not_1_out, not_2_out;
  wire [3:0] register_1_q;

  not not_1 (not_1_out, nLi);
  not not_2 (not_2_out, nEi);
  Register register_1 (.D(in_1), .en(not_1_out), .Q({I7, I6, I5, I4, register_1_q}), .clk(CLK), .clr(CLR));
  assign out_6 = not_2_out ? register_1_q : 4'bz;  // Controlled_Buffer controlled_buffer_1
endmodule

module Acumulador (
  input  [7:0] A_In,
  input  nLa,
  input  CLK,
  input  Ea,
  output [7:0] A_Out_ULA,
  output [7:0] A_Out
);

  wire not_1_out;

  not not_1 (not_1_out, nLa);
  Register register_1 (.D(A_In), .en(not_1_out), .Q(A_Out_ULA), .clk(CLK));  // open: clr
  assign A_Out = Ea ? A_Out_ULA : 8'bz;  // Controlled_Buffer controlled_buffer_1
endmodule

module Somador_Subtrator (
  input  Su,
  input  IncDec,
  input  [7:0] B_data,
  input  [7:0] A_data,
  input  Eu,
  input  mul,
  output [7:0] A_dataOut2
);

  wire not_1_out;
  wire [7:0] adder_1_out, controlled_buffer_1_out, multiplier_1_out, xor_1_out;

  not not_1 (not_1_out, IncDec);
  assign controlled_buffer_1_out = IncDec ? 8'h1 : 8'bz;  // Controlled_Buffer controlled_buffer_1
  assign controlled_buffer_1_out = not_1_out ? B_data : 8'bz;  // Controlled_Buffer controlled_buffer_2
  assign xor_1_out = {8{Su}} ^ controlled_buffer_1_out;  // XOR_Gate xor_1, 8 bits wide
  Adder adder_1 (.a(xor_1_out), .b(A_data), .out(adder_1_out), .cin(Su));  // open: cout
  Multiplier multiplier_1 (.a(B_data), .b(A_data), .out(multiplier_1_out));  // open: cin, cout
  assign A_dataOut2 = Eu ? adder_1_out : 8'bz;  // Controlled_Buffer controlled_buffer_3
  assign A_dataOut2 = mul ? multiplier_1_out : 8'bz;  // Controlled_Buffer controlled_buffer_4
endmodule

module Registrador_B (
  input  [7:0] B_dataIn,
  input  nLb,
  input  CLK,
  output [7:0] B_dataOut
);

  wire not_1_out;

  Register register_1 (.D(B_dataIn), .en(not_1_out), .Q(B_dataOut), .clk(CLK));  // open: clr
  not not_1 (not_1_out, nLb);
endmodule

module Decodificador (
  input  l7,
  input  l6,
  input  l5,
  input  l4,
  output LDA,
  output ADD,
  output SUB,
  output OUT,
  output HLT
);

  wire and_1_out, and_2_out, and_3_out, and_4_out, and_5_out, not_1_out, not_2_out, not_3_out, not_4_out;

  not not_1 (not_1_out, l7);
  not not_2 (not_2_out, l6);
  not not_3 (not_3_out, l5);
  not not_4 (not_4_out, l4);
  and and_1 (and_1_out, not_1_out, not_2_out, not_3_out, not_4_out);
  buf buffer_1 (LDA, and_1_out);
  and and_2 (and_2_out, not_1_out, not_2_out, not_3_out, l4);
  buf buffer_2 (ADD, and_2_out);
  and and_3 (and_3_out, not_1_out, not_2_out, l5, not_4_out);
  buf buffer_3 (SUB, and_3_out);
  buf buffer_4 (OUT, and_4_out);
  and and_4 (and_4_out, l7, l6, l5, not_4_out);
  buf buffer_5 (HLT, and_5_out);
  and and_5 (and_5_out, l7, l6, l5, l4);
endmodule

module \Indicação_Visual  (
  input  [7:0] Input,
  input  nLo,
  input  CLK,
  input  CLR,
  output [7:0] Output
);

  wire not_1_out;

  not not_1 (not_1_out, nLo);
  Register register_1 (.D(Input), .en(not_1_out), .Q(Output), .clk(CLK), .clr(CLR));
endmodule

module Controlador_Sequencializador_ROM (
  input  I7,
  input  I6,
  input  I5,
  input  I4,
  input  CLK,
  input  CLR,
  output loadTmr,
  output Cp,
  output Ep,
  output nLm,
  output nCE,
  output nLl,
  output nEl,
  output nLa,
  output Ea,
  output Su,
  output Eu,
  output nLb,
  output nLo,
  output IncDec,
  output RDnWR,
  output Mul,
  output Lp,
  output lerEnt,
  output HLT
);

  wire and_2_out, and_3_out, and_5_out, and_6_out, clr_t, load, nop, nor_1_out, not_1_out, not_2_out,
       or_1_out, shift_register_1_q0, shift_register_1_q1, shift_register_1_q3, shift_register_1_q4;
  wire [4:0] counter_1_q, rom_1_data;
  wire [15:2] rom_2_data;

  and and_1 (HLT, I7, I6, I5, I4);
  ROM #(.addrWidth(4), .dataWidth(5)) rom_1 (.addr({I7, I6, I5, I4}), .data(rom_1_data));  // open: sel
  or or_1 (or_1_out, CLR, nop);
  or or_2 (clr_t, or_1_out, nor_1_out);
  not not_1 (not_1_out, load);
  not not_2 (not_2_out, CLK);
  Shift_Register #(.length(6)) shift_register_1 (
    .in(nor_1_out), .clk(CLK), .clr(or_1_out), .q0(shift_register_1_q0), .q1(shift_register_1_q1), .q2(load),
    .q3(shift_register_1_q3), .q4(shift_register_1_q4));  // open: shift, out, load, d0, d1, d2, d3, d4, d5, q5
  Counter #(.width(5), .max('h1f), .ongoal("continue")) counter_1 (
    .load(load), .D(rom_1_data), .count(not_1_out), .Q(counter_1_q), .clk(not_2_out), .clr(clr_t));  // open: carry
  nor nor_1 (nor_1_out, shift_register_1_q0, shift_register_1_q1, load, shift_register_1_q3, shift_register_1_q4);
  ROM #(.addrWidth(5), .dataWidth(32)) rom_2 (
    .addr(counter_1_q),
    .data({Cp, Ep, nLm, nCE, nLl, nEl, nLa, Ea, Su, Eu, nLb, nLo, IncDec, RDnWR, Mul, Lp, rom_2_data, lerEnt, loadTmr}));  // open: sel
  and and_2 (and_2_out, ~Cp, ~Ep, nLm, nCE);  // AND_Gate
  and and_3 (and_3_out, nLl, nEl, nLa, ~Ea);  // AND_Gate
  and and_4 (nop, and_2_out, and_3_out, and_5_out, and_6_out);
  and and_5 (and_5_out, ~Su, ~Eu, nLb, nLo);  // AND_Gate
  and and_6 (and_6_out, ~IncDec, ~RDnWR, ~Mul, ~Lp);  // AND_Gate

  // Notes on the sheet:
  //   contents of rom_1 (hex, n*v repeats v):
  //   3 6 9 10 13 16 19 1c 1d 1e 4*0 c
  //   contents of rom_2 (hex, n*v repeats v):
  //   5e300000 be300000 26340000 1a300000 2c340000 3e300000 1a300000 2e140000 3c700000 1a300000 2e140000
  //   3cf00000 3f200000 3e300000 3e300000 0 3c780000 3e300000 3e300000 3cf80000 3e300000 3e300000 1a300000
  //   2e140000 3c320000 3a310000 3e300000 3e300000 1a300000 3e300001 3c300002 3e300000
endmodule

module Cont_Prog (
  input  CLEAR,
  input  EO,
  input  CLK,
  input  CLK_EN,
  input  LOAD,
  input  D0,
  input  D1,
  input  D2,
  input  D3,
  output Q0,
  output Q1,
  output Q2,
  output Q3
);

  wire and_1_out, and_2_out, and_3_out, and_4_out, and_5_out, and_6_out, and_7_out, and_8_out, and_9_out,
       and_10_out, flipflopt_mod_1_q, flipflopt_mod_2_q, flipflopt_mod_3_q, flipflopt_mod_4_q, not_1_out,
       not_2_out, not_3_out, not_4_out;

  and and_1 (and_1_out, LOAD, CLEAR);
  FlipFlopT_mod flipflopt_mod_1 (
    .Toggle(1'b1), .CLK(CLK), .Enable(CLK_EN), .Q(flipflopt_mod_1_q), .Preset(and_1_out), .Set(1'b0),
    .sCLR(and_2_out), .CLR(CLEAR));
  and and_2 (and_2_out, LOAD, not_1_out);
  not not_1 (not_1_out, CLEAR);
  assign Q0 = CLEAR ? flipflopt_mod_1_q : 1'bz;  // Controlled_Buffer controlled_buffer_1
  and and_3 (and_3_out, LOAD, CLEAR);
  FlipFlopT_mod flipflopt_mod_2 (
    .Toggle(flipflopt_mod_1_q), .CLK(CLK), .Enable(CLK_EN), .Q(flipflopt_mod_2_q), .Preset(and_3_out),
    .Set(1'b0), .sCLR(and_4_out), .CLR(CLEAR));
  and and_4 (and_4_out, LOAD, not_2_out);
  not not_2 (not_2_out, CLEAR);
  assign Q1 = CLEAR ? flipflopt_mod_2_q : 1'bz;  // Controlled_Buffer controlled_buffer_2
  and and_5 (and_5_out, flipflopt_mod_1_q, flipflopt_mod_2_q);
  and and_6 (and_6_out, LOAD, CLEAR);
  and and_7 (and_7_out, LOAD, not_3_out);
  not not_3 (not_3_out, CLEAR);
  Controlled_Buffer controlled_buffer_3 (.out(Q2), .en(CLEAR));  // open: in
  FlipFlopT_mod flipflopt_mod_3 (
    .Toggle(and_5_out), .CLK(CLK), .Enable(CLK_EN), .Q(flipflopt_mod_3_q), .Preset(and_6_out), .Set(1'b0),
    .sCLR(and_7_out), .CLR(CLEAR));
  and and_8 (and_8_out, LOAD, D3);
  and and_9 (and_9_out, and_5_out, flipflopt_mod_3_q);
  and and_10 (and_10_out, LOAD, not_4_out);
  assign Q3 = CLEAR ? flipflopt_mod_4_q : 1'bz;  // Controlled_Buffer controlled_buffer_4
  FlipFlopT_mod flipflopt_mod_4 (
    .Toggle(and_9_out), .CLK(CLK), .Enable(CLK_EN), .Q(flipflopt_mod_4_q), .Preset(and_8_out), .Set(1'b0),
    .sCLR(and_10_out), .CLR(CLEAR));
  not not_4 (not_4_out, D3);

  assign D0 = CLEAR;
  assign D1 = CLEAR;
  assign D2 = CLEAR;
  assign EO = CLEAR;
endmodule

module FlipFlopT_mod (
  input  Preset,
  input  Toggle,
  input  Set,
  input  CLK,
  input  Enable,
  input  CLR,
  input  sCLR,
  output Q
);

  wire and_1_out, and_2_out, not_1_out, not_2_out, or_1_out, or_2_out;

  not not_1 (not_1_out, Preset);
  or or_1 (or_1_out, Preset, Toggle);
  not not_2 (not_2_out, sCLR);
  and and_1 (and_1_out, not_1_out, Toggle);
  or or_2 (or_2_out, and_1_out, sCLR);
  and and_2 (and_2_out, or_1_out, not_2_out);
  J_K_Flip_Flop j_k_ff_1 (
    .J(and_2_out), .clk(CLK), .K(or_2_out), .Q(Q), .preset(Set), .en(Enable), .reset(CLR));  // open: Qn
endmodule

module Timer (
  input  CLK,
  input  Ld,
  input  [3:0] Entrada,
  output [3:0] Contador,
  output Reset
);

  wire and_1_out, and_2_out, and_3_out, and_4_out, and_5_out, and_6_out, and_7_out, and_8_out, and_9_out,
       and_10_out, and_11_out, t_ff_1_qn, t_ff_2_qn, t_ff_3_qn;

  and and_1 (and_1_out, CLK, ~Reset);  // AND_Gate
  T_Flip_Flop t_ff_1 (
    .clk(and_1_out), .T(1'b1), .Q(Contador[0]), .Qn(t_ff_1_qn), .preset(and_3_out), .reset(and_2_out));  // open: en
  and and_2 (and_2_out, Ld, ~Entrada[0]);  // AND_Gate
  and and_3 (and_3_out, Entrada[0], Ld);
  T_Flip_Flop t_ff_2 (
    .clk(and_1_out), .T(t_ff_1_qn), .Q(Contador[1]), .Qn(t_ff_2_qn), .preset(and_5_out), .reset(and_4_out));  // open: en
  and and_4 (and_4_out, Ld, ~Entrada[1]);  // AND_Gate
  and and_5 (and_5_out, Entrada[1], Ld);
  and and_6 (and_6_out, t_ff_2_qn, t_ff_1_qn);
  and and_7 (and_7_out, Entrada[2], Ld);
  T_Flip_Flop t_ff_3 (
    .clk(and_1_out), .T(and_6_out), .Q(Contador[2]), .Qn(t_ff_3_qn), .preset(and_7_out), .reset(and_8_out));  // open: en
  and and_8 (and_8_out, Ld, ~Entrada[2]);  // AND_Gate
  and and_9 (and_9_out, t_ff_3_qn, t_ff_2_qn, t_ff_1_qn);
  and and_10 (and_10_out, Entrada[3], Ld);
  T_Flip_Flop t_ff_4 (
    .clk(and_1_out), .T(and_9_out), .Q(Contador[3]), .preset(and_10_out), .reset(and_11_out));  // open: Qn, en
  and and_11 (and_11_out, Ld, ~Entrada[3]);  // AND_Gate
  nor nor_1 (Reset, Contador[0], Contador[1], Contador[2], Contador[3]);

  // Other names for the same wires on the sheet: Zero = Reset

  // Notes on the sheet:
  //   Vídeo de referência: https://www.youtube.com/watch?v=RFwknPtJ_VA
endmodule

module Entrada_8_bits (
  input  rdEnt,
  output [3:0] Endereco,
  output [3:0] Dado,
  output [7:0] Entrada
);

  assign {Dado, Endereco} = rdEnt ? Entrada : 8'bz;  // Controlled_Buffer controlled_buffer_1
endmodule

module Unidade_de_comunicacao (
  input  [7:0] in_1,
  input  ERX,
  input  CLK,
  input  CLR,
  input  Erxout,
  input  [3:0] Tx_barramento1,
  input  [3:0] Tx_barramento2,
  input  LTX,
  output [3:0] rx_barramento1,
  output [3:0] rx_barramento2,
  output [3:0] ligar_display1,
  output [3:0] ligar_display2
);

  wire [7:0] register_1_q;

  Register register_1 (.D(in_1), .en(ERX), .Q(register_1_q), .clk(CLK), .clr(CLR));
  assign {rx_barramento2, rx_barramento1} = Erxout ? register_1_q : 8'bz;  // Controlled_Buffer controlled_buffer_1
  Register register_2 (
    .D({Tx_barramento2, Tx_barramento1}), .en(LTX), .Q({ligar_display2, ligar_display1}), .clk(CLK), .clr(CLR));

  // Notes on the sheet:
  //   TX
  //   Rx
endmodule
